// Logisim project ALU.circ as structural Verilog: 10 circuits, main circuit main
module main (
  input  in_1,
  input  in_2,
  input  S1,
  input  S0
);

  wire A_p1, A_p2, A_p3, A_p4, A_p5, A_p6, A_p7, A_p8, alu_1_aequalb, alu_1_agreaterb, alu_1_alessb,
       alu_1_r0, alu_1_r1, alu_1_r2, alu_1_r3, B_p1, B_p2, B_p3, B_p4, B_p5, B_p6, B_p7, B_p8, encoder_1_a0,
       encoder_1_a1, encoder_1_a2, encoder_1_a3, encoder_2_a0, encoder_2_a1, encoder_2_a2, encoder_2_a3;
  wire [3:0] twos_complementer_1_a0;

  // DipSwitch A: pin names not known; wires that end beside it: A_p1, A_p2, A_p3, A_p4, A_p5, A_p6, A_p7, A_p8
  // DipSwitch B: pin names not known; wires that end beside it: B_p1, B_p2, B_p3, B_p4, B_p5, B_p6, B_p7, B_p8
  Encoder encoder_1 (
    .x1(A_p1), .x2(A_p2), .x3(A_p3), .x4(A_p4), .x5(A_p5), .x6(A_p6), .x7(A_p7), .x8(A_p8), .Sign(in_1),
    .a0(encoder_1_a0), .a1(encoder_1_a1), .a2(encoder_1_a2), .a3(encoder_1_a3));
  Encoder encoder_2 (
    .x1(B_p1), .x2(B_p2), .x3(B_p3), .x4(B_p4), .x5(B_p5), .x6(B_p6), .x7(B_p7), .x8(B_p8), .Sign(in_2),
    .a0(encoder_2_a0), .a1(encoder_2_a1), .a2(encoder_2_a2), .a3(encoder_2_a3));
  ALU alu_1 (
    .a0(encoder_1_a0), .a1(encoder_1_a1), .a2(encoder_1_a2), .a3(encoder_1_a3), .b0(encoder_2_a0),
    .b1(encoder_2_a1), .b2(encoder_2_a2), .b3(encoder_2_a3), .S1(S1), .So(S0), .R0(alu_1_r0), .R1(alu_1_r1),
    .R2(alu_1_r2), .R3(alu_1_r3), .AgreaterB(alu_1_agreaterb), .AequalB(alu_1_aequalb), .AlessB(alu_1_alessb));  // open: V
  TWOs_Complementer twos_complementer_1 (
    .x0(alu_1_r0), .x1(alu_1_r1), .x2(alu_1_r2), .x3(alu_1_r3), .Sign(alu_1_r3),
    .a0(twos_complementer_1_a0[0]), .a1(twos_complementer_1_a0[1]), .a2(twos_complementer_1_a0[2]),
    .a3(twos_complementer_1_a0[3]));
  Hex_Digit_Display hex_digit_display_1 (.value(twos_complementer_1_a0));  // open: dp
  _7_Segment_Display u_7_segment_display_1 (
    .g(alu_1_aequalb), .a(alu_1_agreaterb), .d(alu_1_alessb));  // open: f, b, e, c, dp
endmodule

module OneBitFullAdder (
  input  A,
  input  B,
  input  Ci,
  output Sum,
  output Co
);

  wire and_1_out, and_2_out, xor_1_out;

  xor xor_1 (xor_1_out, A, B);
  and and_1 (and_1_out, xor_1_out, Ci);
  and and_2 (and_2_out, A, B);
  xor xor_2 (Sum, xor_1_out, Ci);
  or or_1 (Co, and_1_out, and_2_out);
endmodule

module OneBitHalfAdder (
  input  A,
  input  C0,
  output X,
  output C1
);

  and and_1 (C1, A, C0);
  xor xor_1 (X, A, C0);
endmodule

module Overflow_Detector (
  input  A3,
  input  B3,
  input  R3,
  output V
);

  wire and_1_out, and_2_out, not_1_out, not_2_out, not_3_out;

  not not_1 (not_1_out, B3);
  not not_2 (not_2_out, R3);
  not not_3 (not_3_out, A3);
  and and_1 (and_1_out, A3, B3, not_2_out);
  and and_2 (and_2_out, not_3_out, not_1_out, R3);
  or or_1 (V, and_1_out, and_2_out);
endmodule

module Adder_Subtractor (
  input  [3:0] A,
  input  [3:0] B,
  input  S0,
  output R0,
  output R1,
  output R2,
  output R3,
  output V
);

  wire Sum0_co, Sum1_co, Sum2_co, Sum3_co, xor_1_out, xor_2_out, xor_3_out, xor_4_out;

  xor xor_1 (xor_1_out, B[0], S0);
  xor xor_2 (xor_2_out, B[1], S0);
  xor xor_3 (xor_3_out, B[2], S0);
  xor xor_4 (xor_4_out, B[3], S0);
  OneBitFullAdder Sum0 (.A(A[0]), .B(xor_1_out), .Ci(S0), .Sum(R0), .Co(Sum0_co));
  OneBitFullAdder Sum1 (.A(A[1]), .B(xor_2_out), .Ci(Sum0_co), .Sum(R1), .Co(Sum1_co));
  OneBitFullAdder Sum2 (.A(A[2]), .B(xor_3_out), .Ci(Sum1_co), .Sum(R2), .Co(Sum2_co));
  OneBitFullAdder Sum3 (.A(A[3]), .B(xor_4_out), .Ci(Sum2_co), .Sum(R3), .Co(Sum3_co));
  Overflow_Detector overflow_detector_1 (.A3(A[2]), .B3(B[3]), .R3(Sum3_co), .V(V));
endmodule

module Magnitude_Comparator (
  input  [3:0] A,
  input  [3:0] B,
  output AgreaterB,
  output AequalB,
  output AlessB
);

  wire and_1_out, and_2_out, and_3_out, and_4_out, and_5_out, and_6_out, and_7_out, and_8_out, not_1_out,
       not_2_out, not_3_out, not_4_out, not_5_out, not_6_out, not_7_out, not_8_out, xnor_1_out, xnor_2_out,
       xnor_3_out, xnor_4_out;

  not not_1 (not_1_out, B[0]);
  not not_2 (not_2_out, B[1]);
  not not_3 (not_3_out, B[2]);
  not not_4 (not_4_out, B[3]);
  xnor xnor_1 (xnor_1_out, A[0], B[0]);
  xnor xnor_2 (xnor_2_out, A[1], B[1]);
  xnor xnor_3 (xnor_3_out, A[2], B[2]);
  xnor xnor_4 (xnor_4_out, A[3], B[3]);
  not not_5 (not_5_out, A[3]);
  not not_6 (not_6_out, A[2]);
  not not_7 (not_7_out, A[1]);
  not not_8 (not_8_out, A[0]);
  and and_1 (and_1_out, A[0], not_1_out, xnor_2_out, xnor_3_out, xnor_4_out);
  and and_2 (and_2_out, A[1], not_2_out, xnor_3_out, xnor_4_out);
  and and_3 (and_3_out, A[2], not_3_out, xnor_4_out);
  and and_4 (and_4_out, A[3], not_4_out);
  and and_5 (and_5_out, B[3], not_5_out);
  and and_6 (and_6_out, xnor_4_out, B[2], not_6_out);
  and and_7 (and_7_out, xnor_4_out, xnor_3_out, B[1], not_7_out);
  and and_8 (and_8_out, xnor_4_out, xnor_3_out, xnor_2_out, B[0], not_8_out);
  or or_1 (AgreaterB, and_1_out, and_2_out, and_3_out, and_4_out);
  and and_9 (AequalB, xnor_1_out, xnor_2_out, xnor_3_out, xnor_4_out);
  or or_2 (AlessB, and_5_out, and_6_out, and_7_out, and_8_out);
endmodule

module TWOs_Complementer (
  input  x0,
  input  x1,
  input  x2,
  input  x3,
  input  Sign,
  output a0,
  output a1,
  output a2,
  output a3
);

  wire onebithalfadder_1_c1, onebithalfadder_2_c1, onebithalfadder_3_c1, xor_1_out, xor_2_out, xor_3_out,
       xor_4_out;

  xor xor_1 (xor_1_out, x0, Sign);
  xor xor_2 (xor_2_out, x1, Sign);
  xor xor_3 (xor_3_out, x2, Sign);
  xor xor_4 (xor_4_out, x3, Sign);
  OneBitHalfAdder onebithalfadder_1 (.A(xor_1_out), .C0(Sign), .X(a0), .C1(onebithalfadder_1_c1));
  OneBitHalfAdder onebithalfadder_2 (.A(xor_2_out), .C0(onebithalfadder_1_c1), .X(a1), .C1(onebithalfadder_2_c1));
  OneBitHalfAdder onebithalfadder_3 (.A(xor_3_out), .C0(onebithalfadder_2_c1), .X(a2), .C1(onebithalfadder_3_c1));
  OneBitHalfAdder onebithalfadder_4 (.A(xor_4_out), .C0(onebithalfadder_3_c1), .X(a3));  // open: C1
endmodule

module Encoder (
  input  x1,
  input  x2,
  input  x3,
  input  x4,
  input  x5,
  input  x6,
  input  x7,
  input  x8,
  input  Sign,
  output a0,
  output a1,
  output a2,
  output a3
);

  wire or_1_out, or_2_out, or_3_out;

  or or_1 (or_1_out, x1, x3, x5, x7);
  or or_2 (or_2_out, x2, x3, x6, x7);
  or or_3 (or_3_out, x4, x5, x6, x7);
  TWOs_Complementer twos_complementer_1 (
    .x0(or_1_out), .x1(or_2_out), .x2(or_3_out), .x3(x8), .Sign(Sign), .a0(a0), .a1(a1), .a2(a2), .a3(a3));
endmodule

module ALU (
  input  a0,
  input  a1,
  input  a2,
  input  a3,
  input  b0,
  input  b1,
  input  b2,
  input  b3,
  input  S1,
  input  So,
  output R0,
  output R1,
  output R2,
  output R3,
  output V,
  output AgreaterB,
  output AequalB,
  output AlessB
);

  wire [3:0] demultiplexer_1_out0, demultiplexer_1_out1, demultiplexer_2_out0, demultiplexer_2_out1;

  Demultiplexer #(.width(4)) demultiplexer_1 (
    .out0(demultiplexer_1_out0), .out1(demultiplexer_1_out1), .in({a3, a2, a1, a0}), .sel(S1));
  Demultiplexer #(.width(4)) demultiplexer_2 (
    .out0(demultiplexer_2_out0), .out1(demultiplexer_2_out1), .in({b3, b2, b1, b0}), .sel(S1));
  Adder_Subtractor Sum_Difference (
    .A(demultiplexer_1_out0), .B(demultiplexer_2_out0), .S0(So), .R0(R0), .R1(R1), .R2(R2), .R3(R3), .V(V));
  Magnitude_Comparator Comparision (
    .A(demultiplexer_1_out1), .B(demultiplexer_2_out1), .AgreaterB(AgreaterB), .AequalB(AequalB),
    .AlessB(AlessB));
endmodule

module Sum_Decoder (
  input  in_1,
  input  in_2,
  input  in_3,
  input  in_4
);

  wire and_1_out, and_2_out, and_3_out, and_4_out, not_1_out, not_2_out, not_3_out, not_4_out;

  and and_1 (and_1_out, in_1, in_3);
  and and_2 (and_2_out, in_1, in_2);
  not not_1 (not_1_out, in_1);
  not not_2 (not_2_out, in_2);
  not not_3 (not_3_out, in_3);
  not not_4 (not_4_out, in_4);
  and and_3 (and_3_out, not_1_out, not_3_out);
  and and_4 (and_4_out, not_1_out, not_2_out);
  // OR_Gate or_1 has open pins: in0=in_2, in1=and_1_out, in2=and_3_out, in3=in_4, out=open
  // OR_Gate or_2 has open pins: in0=and_2_out, in1=and_4_out, in2=not_3_out, out=open
  // OR_Gate or_3 has open pins: in0=in_3, in1=in_1, in2=not_2_out, out=open
endmodule
